// Digital circuit latch_RS.dig as structural Verilog
module latch_RS (
  input  R,
  input  S,
  input  R_2,
  input  S_2,
  input  C,
  input  D,
  input  C_2,
  input  D_2,
  input  C_3,
  input  R_3,
  output Q,
  output nQ,
  output Q_2,
  output nQ_2,
  output Q_3,
  output nQ_3,
  output Q_4,
  output Q_5,
  output nQ_4
);

  wire and_1_out, and_2_out, and_3_out, and_4_out, and_5_out, and_6_out, and_7_out, and_8_out, nor_7_out,
       nor_8_out, nor_10_out, not_1_out, not_2_out, not_3_out, not_4_out;

  nor nor_1 (Q_5, R_3, nQ_4);
  nor nor_2 (nQ_4, Q_5, R_3);
  not not_1 (not_1_out, D_2);
  and and_1 (and_1_out, R_2, C);
  and and_2 (and_2_out, C, S_2);
  and and_3 (and_3_out, not_1_out, C_3);
  and and_4 (and_4_out, C_3, D_2);
  nor nor_3 (Q, R, nQ);
  nor nor_4 (nQ, Q, S);
  nor nor_5 (Q_2, and_1_out, nQ_2);
  nor nor_6 (nQ_2, Q_2, and_2_out);
  nor nor_7 (nor_7_out, and_3_out, nor_8_out);
  nor nor_8 (nor_8_out, nor_7_out, and_4_out);
  not not_2 (not_2_out, C_3);
  not not_3 (not_3_out, nor_7_out);
  and and_5 (and_5_out, not_3_out, not_2_out);
  and and_6 (and_6_out, not_2_out, nor_7_out);
  not not_4 (not_4_out, D);
  and and_7 (and_7_out, not_4_out, C_2);
  and and_8 (and_8_out, C_2, D);
  nor nor_9 (Q_4, and_5_out, nor_10_out);
  nor nor_10 (nor_10_out, Q_4, and_6_out);
  nor nor_11 (Q_3, and_7_out, nQ_3);
  nor nor_12 (nQ_3, Q_3, and_8_out);
endmodule
