// Digital circuit registers.dig as structural Verilog
module registers (
  input  in_1,
  input  in_2,
  input  in_3,
  input  in_4,
  input  in_5,
  input  clk,
  input  in_7,
  input  clk_2,
  input  clk_3,
  input  in_10,
  input  DIN,
  input  in_12,
  input  in_13,
  input  in_14,
  input  in_15,
  input  in_16,
  input  LOAD,
  input  CLK_4
);

  wire d_ff_1_q, d_ff_2_q, d_ff_3_q, d_ff_4_q, d_ff_5_q, d_ff_6_q, d_ff_7_q, d_ff_8_q, d_ff_9_q, d_ff_10_q,
       d_ff_11_q, d_ff_12_q, d_ff_13_q, d_ff_14_q, d_ff_15_q, d_ff_16_q, d_ff_17_q, d_ff_18_q, d_ff_19_q,
       d_ff_20_q, multiplexer_1_out, multiplexer_2_out, multiplexer_3_out, multiplexer_4_out,
       multiplexer_5_out;

  D_FF d_ff_1 (.D(in_1), .C(clk), .Q(d_ff_1_q));  // open: nQ
  D_FF d_ff_2 (.D(in_2), .C(clk), .Q(d_ff_2_q));  // open: nQ
  D_FF d_ff_3 (.D(in_3), .C(clk), .Q(d_ff_3_q));  // open: nQ
  D_FF d_ff_4 (.D(in_4), .C(clk), .Q(d_ff_4_q));  // open: nQ
  D_FF d_ff_5 (.D(in_5), .C(clk), .Q(d_ff_5_q));  // open: nQ
  Multiplexer multiplexer_1 (.sel(LOAD), .in_0(in_12), .in_1(DIN), .out(multiplexer_1_out));
  // Probe A on d_ff_1_q
  // Probe B on d_ff_2_q
  // Probe C on d_ff_3_q
  // Probe D on d_ff_4_q
  // Probe E on d_ff_5_q
  // Probe ASLL on d_ff_6_q
  D_FF d_ff_6 (.D(multiplexer_1_out), .C(CLK_4), .Q(d_ff_6_q));  // open: nQ
  Multiplexer multiplexer_2 (.sel(LOAD), .in_0(in_13), .in_1(d_ff_6_q), .out(multiplexer_2_out));
  // Probe BSLL on d_ff_7_q
  D_FF d_ff_7 (.D(multiplexer_2_out), .C(CLK_4), .Q(d_ff_7_q));  // open: nQ
  // Probe ASL on d_ff_8_q
  D_FF d_ff_8 (.D(d_ff_9_q), .C(clk_2), .Q(d_ff_8_q));  // open: nQ
  // Probe BSL on d_ff_9_q
  D_FF d_ff_9 (.D(d_ff_10_q), .C(clk_2), .Q(d_ff_9_q));  // open: nQ
  Multiplexer multiplexer_3 (.sel(LOAD), .in_0(in_14), .in_1(d_ff_7_q), .out(multiplexer_3_out));
  // Probe CSL on d_ff_10_q
  D_FF d_ff_10 (.D(d_ff_12_q), .C(clk_2), .Q(d_ff_10_q));  // open: nQ
  // Probe CSLL on d_ff_11_q
  D_FF d_ff_11 (.D(multiplexer_3_out), .C(CLK_4), .Q(d_ff_11_q));  // open: nQ
  // Probe DSL on d_ff_12_q
  D_FF d_ff_12 (.D(d_ff_13_q), .C(clk_2), .Q(d_ff_12_q));  // open: nQ
  Multiplexer multiplexer_4 (.sel(LOAD), .in_0(in_15), .in_1(d_ff_11_q), .out(multiplexer_4_out));
  // Probe ESL on d_ff_13_q
  D_FF d_ff_13 (.D(in_7), .C(clk_2), .Q(d_ff_13_q));  // open: nQ
  // Probe DSLL on d_ff_14_q
  D_FF d_ff_14 (.D(multiplexer_4_out), .C(CLK_4), .Q(d_ff_14_q));  // open: nQ
  Multiplexer multiplexer_5 (.sel(LOAD), .in_0(in_16), .in_1(d_ff_14_q), .out(multiplexer_5_out));
  // Probe ASR on d_ff_15_q
  D_FF d_ff_15 (.D(in_10), .C(clk_3), .Q(d_ff_15_q));  // open: nQ
  // Probe BSR on d_ff_16_q
  D_FF d_ff_16 (.D(d_ff_15_q), .C(clk_3), .Q(d_ff_16_q));  // open: nQ
  // Probe ESLL on d_ff_17_q
  D_FF d_ff_17 (.D(multiplexer_5_out), .C(CLK_4), .Q(d_ff_17_q));  // open: nQ
  // Probe CSR on d_ff_18_q
  D_FF d_ff_18 (.D(d_ff_16_q), .C(clk_3), .Q(d_ff_18_q));  // open: nQ
  // Probe DSR on d_ff_19_q
  D_FF d_ff_19 (.D(d_ff_18_q), .C(clk_3), .Q(d_ff_19_q));  // open: nQ
  // Probe ESR on d_ff_20_q
  D_FF d_ff_20 (.D(d_ff_19_q), .C(clk_3), .Q(d_ff_20_q));  // open: nQ
endmodule
